// Logisim project decodificador.circ as structural Verilog: 2 circuits, main circuit main
module main (
  input  A3,
  input  A2,
  input  A1,
  input  A0
);

  wire decodificadorrunico_1_a, decodificadorrunico_1_b, decodificadorrunico_1_c, decodificadorrunico_1_d,
       decodificadorrunico_1_e, decodificadorrunico_1_f, decodificadorrunico_1_g;

  decodificadorRunico decodificadorrunico_1 (
    .A3(A3), .A2(A2), .A1(A1), .A0(A0), .a(decodificadorrunico_1_a), .b(decodificadorrunico_1_b),
    .c(decodificadorrunico_1_c), .d(decodificadorrunico_1_d), .e(decodificadorrunico_1_e),
    .f(decodificadorrunico_1_f), .g(decodificadorrunico_1_g));
  _7_Segment_Display u_7_segment_display_1 (
    .g(decodificadorrunico_1_g), .f(decodificadorrunico_1_f), .a(decodificadorrunico_1_a),
    .b(decodificadorrunico_1_b), .e(decodificadorrunico_1_e), .d(decodificadorrunico_1_d),
    .c(decodificadorrunico_1_c));  // open: dp
endmodule

module decodificadorRunico (
  input  A3,
  input  A2,
  input  A1,
  input  A0,
  output a,
  output b,
  output c,
  output d,
  output e,
  output f,
  output g
);

  wire and_1_out, and_2_out, and_3_out, and_4_out, and_5_out, and_6_out, and_7_out, and_8_out, and_9_out,
       and_10_out, and_11_out, and_12_out, and_13_out, and_14_out, and_15_out, and_16_out, and_17_out,
       and_18_out, and_19_out, and_20_out, and_21_out, and_22_out, and_23_out, and_24_out, and_25_out,
       not_1_out, not_2_out, not_3_out, not_4_out;

  not not_1 (not_1_out, A3);
  not not_2 (not_2_out, A2);
  not not_3 (not_3_out, A1);
  not not_4 (not_4_out, A0);
  and and_1 (and_1_out, not_1_out, not_2_out, not_4_out);
  and and_2 (and_2_out, A3, A0);
  and and_3 (and_3_out, not_1_out, A2, not_3_out);
  and and_4 (and_4_out, not_2_out, A1);
  and and_5 (and_5_out, A1, not_4_out);
  and and_6 (and_6_out, A2, A0);
  and and_7 (and_7_out, A2, A1);
  and and_8 (and_8_out, not_1_out, A1);
  and and_9 (and_9_out, not_3_out, not_4_out);
  and and_10 (and_10_out, A2, not_4_out);
  and and_11 (and_11_out, A3, not_2_out, A0);
  and and_12 (and_12_out, not_1_out, not_2_out, A0);
  and and_13 (and_13_out, A3, not_3_out);
  and and_14 (and_14_out, not_1_out, A2, not_3_out, A0);
  and and_15 (and_15_out, A3, A2, not_4_out);
  and and_16 (and_16_out, A3, A1);
  and and_17 (and_17_out, A1, A0);
  and and_18 (and_18_out, not_1_out, A2, not_4_out);
  and and_19 (and_19_out, A3, not_2_out);
  and and_20 (and_20_out, not_1_out, not_3_out, not_4_out);
  and and_21 (and_21_out, not_1_out, A0);
  and and_22 (and_22_out, A2, not_3_out);
  and and_23 (and_23_out, A3, not_4_out);
  and and_24 (and_24_out, not_2_out, not_4_out);
  and and_25 (and_25_out, A3, A1);
  or or_1 (a, and_1_out, and_6_out, and_2_out, and_7_out, and_8_out);
  or or_2 (b, and_9_out, and_3_out, and_10_out, and_11_out);
  or or_3 (c, and_5_out, and_12_out, and_13_out);
  or or_4 (d, and_1_out, and_4_out, and_14_out, and_5_out, and_15_out, and_16_out);
  or or_5 (e, and_17_out, and_2_out, and_18_out, and_19_out, and_20_out);
  or or_6 (f, and_21_out, and_4_out, and_22_out, and_23_out);
  or or_7 (g, and_24_out, and_25_out, and_3_out, and_2_out);
endmodule
